# Fritzing sketch EspNeoPixelConnection (saved by Fritzing 0.9.2b)
breadboards: 1

parts:
  NEOPIXEL1 = Neopixel Strip -- Black (30/m)
  U1 = NodeMCU V1.0
  R2 = Resistor [tolerance=±5% resistance=220 package=THT]
  JACK1 = 2.1mm Barrel Jack with Terminal Block
  C3 = Capacitor Polarized [package=nippon_f80]

nets:
  GND: NEOPIXEL1.GND, U1.GND, JACK1.NEG, C3.-
  N1: NEOPIXEL1.Din, R2.Pin_0
  N2: NEOPIXEL1.+5V, C3.+
  N3: U1.RX, R2.Pin_1

notes:
  https://github.com/krzychb/EspFire2012
  =4.5V DC
  WS2812B, 144 LED/m
  1000µF / 16V
  470Ω

custom parts:
  Neopixel Strip -- Black (30/m): These NeoPixel strips have 30 digitally-addressable pixel LEDs per meter and are very affordable and are only 12.5 mm wide, 10 mm if you remove the strip from the casing.
  NodeMCU V1.0: ESP9266 based NodeMCU
